# Fritzing sketch Connection (saved by Fritzing 1.0.7)

parts:
  Adafruit_INA228_I2C_Power_Monitor1 = Adafruit INA228 I2C Power Monitor [mn=Adafruit mpn=#5832 part_number=#5832]
  Part1 = XBee Pro RF module
  Leawood_Power_Sensor_1 = Leawood Power Sensor 1

nets:
  N1: Adafruit_INA228_I2C_Power_Monitor1.SCL, Leawood_Power_Sensor_1./SCL
  N2: Adafruit_INA228_I2C_Power_Monitor1.VCC, Leawood_Power_Sensor_1.+3.3V#0
  N3: Adafruit_INA228_I2C_Power_Monitor1.GND, Leawood_Power_Sensor_1.GND#1
  N4: Adafruit_INA228_I2C_Power_Monitor1.SDA, Leawood_Power_Sensor_1./SDA
  N5: Part1.VCC, Leawood_Power_Sensor_1.+3.3V#12
  N6: Part1.DOUT, Leawood_Power_Sensor_1./RxD0
  N7: Part1.DIN, Leawood_Power_Sensor_1./TxD0
  N8: Part1.RESET, Leawood_Power_Sensor_1./MODEM_RESET
  N9: Part1.GND, Leawood_Power_Sensor_1.GND#13
  N10: Part1.ON/SLEEP, Leawood_Power_Sensor_1./MODEM_SLEEP

custom parts:
  Leawood Power Sensor 1: Auto-generated starter part from KiCad board connector model.
